// Logisim project CMP.circ as structural Verilog: 1 circuit, main circuit main
// CMP
module main (
  input  LT,
  input  EQ,
  input  GT,
  input  [2:0] CQ_QUERY,
  input  CR_WRITE,
  input  CLOCK,
  output [2:0] CR_VAL,
  output CQ_PASSED
);

  wire CR_WRITE_t, not_1_out, or_1_out, or_2_out;

  Comparator #(.width(1)) comparator_1 (.a(GT), .b(CQ_QUERY[0]));  // open: gt, eq, lt
  Comparator #(.width(1)) comparator_2 (.a(CQ_QUERY[1]), .b(EQ));  // open: gt, eq, lt
  Comparator #(.width(1)) comparator_3 (.a(CQ_QUERY[2]), .b(LT));  // open: gt, eq, lt
  Multiplexer #(.select(2)) multiplexer_1 (.in0(LT), .in2(EQ), .in3(GT));  // open: in1, out, sel, en
  Register #(.width(3)) CQ_Register (.en(CR_WRITE_t), .clk(CLOCK));  // open: D, Q, clr
  Multiplexer #(.select(3), .enable("false")) multiplexer_2 (.sel(CR_VAL));  // open: in0, in1, in2, in3, in4, in5, in6, in7, out
  or or_1 (or_1_out, EQ, GT);
  not not_1 (not_1_out, EQ);
  or or_2 (or_2_out, EQ, LT);

  // Other names for the same wires on the sheet: clk = CLOCK; tunnel = LT; tunnel_t = EQ; tunnel_t_t = GT

  // Notes on the sheet:
  //   CR MODULE
endmodule
