// Logisim project CPU.circ as structural Verilog: 1 circuit, main circuit main
// CPU
module main (
  input  [31:0] INSTRUCTION,
  input  [23:0] CURRENT_PC,
  input  CQ_PASSED,
  input  [31:0] REG_1_VAL,
  input  [31:0] REG_2_VAL,
  input  [31:0] REG_3_VAL,
  input  [31:0] ALU_RESULT,
  input  [31:0] MEM_OUT,
  output [23:0] JUMP_ADDRESS,
  output [2:0] CQ_QUERY,
  output CR_WRITE,
  output [3:0] REG_1_READ,
  output [3:0] REG_2_READ,
  output [3:0] REG_3_WRITE,
  output [31:0] REG_WRITE_VAL,
  output REG_WRITE,
  output [31:0] ALU_SOURCE_X,
  output [31:0] ALU_SOURCE_Y,
  output [3:0] ALU_OPERATION,
  output [23:0] MEM_ADDR,
  output [31:0] MEM_IN,
  output MEM_WRITE,
  output SHL,
  output SHR,
  output AND,
  output IOR,
  output XOR,
  output STU,
  output MUL,
  output DIV,
  output SUB,
  output ADD,
  output MLD,
  output MST,
  output STL,
  output CMP,
  output LNK,
  output JMP
);

  wire ALUop, clk, comparator_1_eq, comparator_2_eq, comparator_3_eq, comparator_4_eq, comparator_6_eq,
       comparator_7_lt, CQ_Cmd, CQ_Output, Jump_Cmd, Link_Cmd, Load_Cmd, memWrite, not_1_out, not_2_out,
       not_3_out, not_4_out, not_5_out, not_6_out, not_7_out, not_8_out, or_1_out, prev_jump, write;
  wire [1:0] A_Type;
  wire [31:0] multiplexer_1_out, shifter_1_out;

  // OR_Gate MemtoReg is placed but not wired
  Shifter #(.width(32), .shift("lr")) shifter_1 (.in(INSTRUCTION), .\dist (5'b11100), .out(shifter_1_out));
  Bit_Extender #(.in_width(32), .out_width(4)) bit_extender_1 (.in(shifter_1_out), .out(ALU_OPERATION));
  Multiplexer #(.select(2), .width(32), .enable("false")) multiplexer_1 (
    .in0(REG_1_VAL), .in1(REG_2_VAL), .in3(REG_3_VAL), .out(multiplexer_1_out));  // open: in2, sel
  // OR_Gate RegWrite is placed but not wired
  or ALUSrc (ALUop, AND, IOR, XOR, STU, MUL, DIV, SUB, ADD, STL);
  // OR_Gate RegDst has open pins: in0=SHL, in1=SHR, in2=AND, in3=IOR, in4=XOR, in5=STU, in6=MUL, in7=DIV, in8=SUB, in9=ADD, in10=MLD, in11=MST, in12=STL, in13=CMP, in14=LNK, out=open
  // OR_Gate nPC_sel is placed but not wired
  // OR_Gate ExtOp is placed but not wired
  // OR_Gate ALUctr_0 is placed but not wired
  // OR_Gate ALUctr_1 is placed but not wired
  not not_1 (not_1_out, ALU_OPERATION[0]);
  not not_2 (not_2_out, ALU_OPERATION[1]);
  not not_3 (not_3_out, ALU_OPERATION[2]);
  not not_4 (not_4_out, ALU_OPERATION[3]);
  buf u_MemWrite (MEM_WRITE, MST);  // OR_Gate
  not not_5 (not_5_out, ALU_OPERATION[0]);
  not not_6 (not_6_out, ALU_OPERATION[1]);
  not not_7 (not_7_out, ALU_OPERATION[2]);
  not not_8 (not_8_out, ALU_OPERATION[3]);
  and u_SHL (SHL, not_1_out, not_2_out, not_3_out, not_4_out);
  Comparator #(.width(4), .mode("unsigned")) comparator_1 (
    .a(ALU_OPERATION), .b(4'b1111), .eq(comparator_1_eq));  // open: gt, lt
  Comparator #(.width(4), .mode("unsigned")) comparator_2 (
    .a(ALU_OPERATION), .b(4'b1010), .eq(comparator_2_eq));  // open: gt, lt
  Comparator #(.width(4), .mode("unsigned")) comparator_3 (
    .a(ALU_OPERATION), .b(4'b1011), .eq(comparator_3_eq));  // open: gt, lt
  // AND_Gate and_1 has open pins: in0=ALU_OPERATION[0], in1=not_6_out, in2=ALU_OPERATION[2], in3=ALU_OPERATION[3], out=open
  and u_SHR (SHR, ALU_OPERATION[0], not_2_out, not_3_out, not_4_out);
  and and_2 (Jump_Cmd, comparator_1_eq, prev_jump, CQ_Output);
  and and_3 (Load_Cmd, comparator_2_eq, prev_jump, CQ_Output);
  and and_4 (memWrite, comparator_3_eq, prev_jump, CQ_Output);
  // AND_Gate and_5 is placed but not wired
  and AND_6 (AND, not_1_out, ALU_OPERATION[0], not_3_out, not_4_out);
  and u_IOR (IOR, ALU_OPERATION[0], ALU_OPERATION[1], not_3_out, not_4_out);
  Comparator #(.width(32)) comparator_4 (.a(32'hf), .eq(comparator_4_eq));  // open: b, gt, lt
  and u_XOR (XOR, not_1_out, not_2_out, ALU_OPERATION[2], not_4_out);
  and u_STU (STU, ALU_OPERATION[0], not_3_out, ALU_OPERATION[2], not_4_out);
  and u_MUL (MUL, not_1_out, ALU_OPERATION[1], ALU_OPERATION[2], not_4_out);
  Comparator #(.width(4), .mode("unsigned")) comparator_5 (
    .a(ALU_OPERATION), .b(4'b1110), .eq(Link_Cmd));  // open: gt, lt
  and u_DIV (DIV, ALU_OPERATION[0], ALU_OPERATION[1], ALU_OPERATION[2], not_4_out);
  Comparator #(.width(2)) comparator_6 (.a(2'b01), .b(A_Type), .eq(comparator_6_eq));  // open: gt, lt
  Comparator #(.width(4), .mode("unsigned")) comparator_7 (
    .a(ALU_OPERATION), .b(4'b1011), .lt(comparator_7_lt));  // open: gt, eq
  and u_SUB (SUB, not_1_out, not_2_out, not_3_out, ALU_OPERATION[3]);
  and and_7 (CQ_Cmd, comparator_6_eq, prev_jump, CQ_Output);
  or or_1 (or_1_out, comparator_7_lt, Link_Cmd);
  and u_ADD (ADD, ALU_OPERATION[0], not_2_out, not_3_out, ALU_OPERATION[3]);
  and and_8 (write, CQ_Output, prev_jump, clk, or_1_out);
  and u_MST (MST, ALU_OPERATION[0], not_2_out, not_3_out, ALU_OPERATION[3]);
  and u_MLD (MLD, not_1_out, ALU_OPERATION[1], not_3_out, ALU_OPERATION[3]);
  and u_STL (STL, not_1_out, not_3_out, ALU_OPERATION[2], ALU_OPERATION[3]);
  and u_CMP (CMP, ALU_OPERATION[0], not_2_out, ALU_OPERATION[2], ALU_OPERATION[3]);
  and u_LNK (LNK, not_1_out, ALU_OPERATION[1], ALU_OPERATION[2], ALU_OPERATION[3]);
  and u_JMP (JMP, ALU_OPERATION[0], ALU_OPERATION[1], ALU_OPERATION[2], ALU_OPERATION[3]);

  // Other names for the same wires on the sheet: MEM_ID[31:0] = MEM_IN; memStore = MEM_WRITE; Save_Cmd = memWrite;
  //   OP_Code[3:0] = ALU_OPERATION

  // Notes on the sheet:
  //   INSTRUCTION MODULE
  //   CR MODULE
  //   REGISTER FILE MODULE
  //   ALU MODULE
  //   MEMORY MODULE
  //   Control
  //   Can REG write?
  //   Is this  set CQ command?
endmodule
