// Logisim project NPC.circ as structural Verilog: 1 circuit, main circuit main
// NPC
module main (
  input  CQ_PASSED,
  input  [31:0] INSTRUCTION,
  input  [23:0] CURRENT_PC,
  input  [23:0] JUMP_ADDRESS,
  output [23:0] NEXT_PC
);

  wire clk, jcontrol, Jump_Cmd, prev_jump, register_1_q;
  wire [4:0] undriven;
  wire [23:0] bit_extender_1_out, pc_q;
  wire [31:0] inst, Instruction_Register_q, shifter_1_out, undriven_2;

  not not_1 (prev_jump, register_1_q);
  Register #(.width(1)) register_1 (.D(Jump_Cmd), .Q(register_1_q), .clk(clk));  // open: en, clr
  Multiplexer #(.width(24), .enable("false")) multiplexer_1 (
    .in0(JUMP_ADDRESS), .out(CURRENT_PC), .sel(jcontrol));  // open: in1
  Register #(.width(32)) Instruction_Register (.D(inst), .en(CQ_PASSED), .Q(Instruction_Register_q));  // open: clk, clr
  assign bit_extender_1_out = {{23{1'b0}}, 1'b1};  // Bit_Extender bit_extender_1
  Register #(.width(24)) pc (.D(CURRENT_PC), .en(CQ_PASSED), .Q(pc_q));  // open: clk, clr
  Shifter #(.width(32), .shift("lr")) shifter_1 (.in(Instruction_Register_q), .\dist (undriven), .out(shifter_1_out));
  Adder #(.width(24)) adder_1 (.a(bit_extender_1_out), .b(pc_q), .out(NEXT_PC));  // open: cin, cout
  Comparator #(.width(32)) comparator_1 (.a(undriven_2), .b(shifter_1_out), .eq(jcontrol));  // open: gt, lt
  // NOT_Gate not_2 has open pins: in=Jump_Cmd, out=open

  // Other names for the same wires on the sheet: cPC[23:0] = CURRENT_PC; cqpass = CQ_PASSED; j[23:0] = JUMP_ADDRESS;
  //   nextPC[23:0] = NEXT_PC

  // Notes on the sheet:
  //   NPC MODULE
endmodule
