// Logisim project PIP.circ as structural Verilog: 1 circuit, main circuit main
// PIP
module main (
  input  CQ_PASSED,
  input  [31:0] INSTRUCTION_IN,
  input  [23:0] PC_IN,
  input  CLOCK,
  output [31:0] INSTRUCTION_OUT,
  output [23:0] PC_OUT
);


  assign INSTRUCTION_OUT = INSTRUCTION_IN;
  assign PC_OUT = PC_IN;

  // Notes on the sheet:
  //   PIPELINE MODULE
endmodule
